# Fritzing sketch carrera_rundenzaehler (saved by Fritzing 0.9.3b)
circuit board: 8.46667cm x 5.64444cm
breadboards: 1

parts:
  Part1 = Adafruit Gemma M0 [part_number="Adafruit #3501"]
  R1 = Resistor [tolerance=±5% resistance=570 package=THT]
  R2 = Resistor [tolerance=±5% resistance=570 package=THT]
  U1 = CNZ1120 [package=cnz1120]
  U2 = CNZ1120 [package=cnz1120]
  R8 = Resistor [tolerance=±5% resistance=1k package=THT]
  R9 = Resistor [tolerance=±5% resistance=1k package=THT]

nets:
  N1: Part1.3.3V, R1.Pin_0, R2.Pin_1, U1.4, U2.4
  N2: Part1.D0_SDA_TX, U1.3, R9.Pin_0
  N3: Part1.D1_A0, U2.3, R8.Pin_1
  N4: Part1.GND, U1.2, U2.2, R8.Pin_0, R9.Pin_1
  N5: R1.Pin_1, U2.1
  N6: R2.Pin_0, U1.1

custom parts:
  Adafruit Gemma M0: The Adafruit Gemma M0 is a super small microcontroller board, with just enough built-in to create many simple projects. It may look small and cute: round, about the size of a quarter, with friendly alligator-clip sew pads. But do not be fooled! The Gemma M0 is incredibly powerful! We've taken the same form factor we used for the original ATtiny85-based Gemma and gave it an upgrade. The Gemma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
